// Logisim project 6522.circ as structural Verilog: 3 circuits, main circuit W65C22
module W65C22 (
  input  [7:0] PORTA_IN,
  input  [3:0] REG_SEL,
  input  [7:0] DATA_IN,
  input  PHI2,
  input  RESB,
  input  CS1,
  input  CS2B,
  input  RWB,
  input  [7:0] PORTB_IN,
  output [7:0] PORTA_OUT,
  output [7:0] DATA_OUT,
  output [7:0] PORTB_OUT,
  output CA1,
  output CA2,
  output CB1,
  output IRQB,
  output CB2
);

  wire and_1_out, and_2_out, and_3_out, and_4_out, and_5_out, and_6_out, and_7_out, and_8_out, and_9_out,
       and_10_out, and_11_out, RESET, RS0, RS1, RS2, RS3;
  wire [7:0] controlled_buffer_2_out, DDRA_q, DDRB_q, IRA_q, IRB_q, ORA_q, ORB_q, port_buffer_1_data_out,
       port_buffer_2_data_out;

  and and_1 (and_1_out, ~RWB, and_3_out);  // AND_Gate
  and and_2 (and_2_out, and_3_out, RWB);
  assign DATA_OUT = and_2_out ? controlled_buffer_2_out : 8'bz;  // Controlled_Buffer controlled_buffer_1
  not not_1 (RESET, RESB);
  Demultiplexer #(.select(4)) demultiplexer_1 (
    .out0(RS0), .out1(RS1), .out2(RS2), .out3(RS3), .in(1'b1), .sel(REG_SEL));  // open: out4, out5, out6, out7, out8, out9, out10, out11, out12, out13, out14, out15
  assign controlled_buffer_2_out = and_1_out ? DATA_IN : 8'bz;  // Controlled_Buffer controlled_buffer_2
  and and_3 (and_3_out, CS1, ~CS2B);  // AND_Gate
  Register T1C_L ();  // open: D, en, clk, Q, clr
  Register T2C_L ();  // open: D, en, clk, Q, clr
  Register PCR ();  // open: D, en, clk, Q, clr
  Register T1C_H ();  // open: D, en, clk, Q, clr
  Register T2C_H ();  // open: D, en, clk, Q, clr
  Register IFR ();  // open: D, en, clk, Q, clr
  Register T1L_L ();  // open: D, en, clk, Q, clr
  Register SR ();  // open: D, en, clk, Q, clr
  Register IER ();  // open: D, en, clk, Q, clr
  Register T1L_H ();  // open: D, en, clk, Q, clr
  Register ACR ();  // open: D, en, clk, Q, clr
  Register ORA_IRA_2 ();  // open: D, en, clk, Q, clr
  and and_4 (and_4_out, RS3, ~RWB);  // AND_Gate
  and and_5 (and_5_out, RS1, ~RWB);  // AND_Gate
  assign controlled_buffer_2_out = and_6_out ? IRA_q : 8'bz;  // Controlled_Buffer controlled_buffer_3
  and and_6 (and_6_out, RWB, RS1);
  and and_7 (and_7_out, RS2, ~RWB);  // AND_Gate
  and and_8 (and_8_out, RS0, ~RWB);  // AND_Gate
  assign controlled_buffer_2_out = and_9_out ? IRB_q : 8'bz;  // Controlled_Buffer controlled_buffer_4
  and and_9 (and_9_out, RWB, RS0);
  Register DDRA (.D(controlled_buffer_2_out), .en(and_4_out), .clk(PHI2), .Q(DDRA_q), .clr(RESET));
  Register ORA (.D(controlled_buffer_2_out), .en(and_5_out), .clk(PHI2), .Q(ORA_q), .clr(RESET));
  Register IRA (.D(port_buffer_1_data_out), .en(1'b1), .clk(PHI2), .Q(IRA_q), .clr(RESET));
  Register DDRB (.D(controlled_buffer_2_out), .en(and_7_out), .clk(PHI2), .Q(DDRB_q), .clr(RESET));
  Register ORB (.D(controlled_buffer_2_out), .en(and_8_out), .clk(PHI2), .Q(ORB_q), .clr(RESET));
  Register IRB (.D(port_buffer_2_data_out), .en(1'b1), .clk(PHI2), .Q(IRB_q), .clr(RESET));
  // NoConnect on CA1
  // NoConnect on CA2
  // NoConnect on CB1
  // NoConnect on CB2
  assign controlled_buffer_2_out = and_10_out ? DDRA_q : 8'bz;  // Controlled_Buffer controlled_buffer_5
  and and_10 (and_10_out, RWB, RS3);
  assign controlled_buffer_2_out = and_11_out ? DDRB_q : 8'bz;  // Controlled_Buffer controlled_buffer_6
  and and_11 (and_11_out, RWB, RS2);
  Port_Buffer port_buffer_1 (
    .DDR(DDRA_q), .DATA_IN(ORA_q), .PORT_IN(PORTA_IN), .PORT_OUT(PORTA_OUT), .DATA_OUT(port_buffer_1_data_out));
  Port_Buffer port_buffer_2 (
    .DDR(DDRB_q), .DATA_IN(ORB_q), .PORT_IN(PORTB_IN), .PORT_OUT(PORTB_OUT), .DATA_OUT(port_buffer_2_data_out));

  // Other names for the same wires on the sheet: CLK = PHI2
endmodule

module Port_Buffer (
  input  [7:0] DDR,
  input  [7:0] DATA_IN,
  input  [7:0] PORT_IN,
  output [7:0] PORT_OUT,
  output [7:0] DATA_OUT
);

  Transistor_Test transistor_test_1 (
    .DDR(DDR[0]), .DATA(DATA_IN[0]), .PIN_IN(PORT_IN[0]), .PIN_OUT(PORT_OUT[0]), .DATA_IN(DATA_OUT[0]));
  Pull_Resistor pull_resistor_1 (.node(DATA_OUT[0]));
  Transistor_Test transistor_test_2 (
    .DDR(DDR[1]), .DATA(DATA_IN[1]), .PIN_IN(PORT_IN[1]), .PIN_OUT(PORT_OUT[1]), .DATA_IN(DATA_OUT[1]));
  Pull_Resistor pull_resistor_2 (.node(DATA_OUT[1]));
  Transistor_Test transistor_test_3 (
    .DDR(DDR[2]), .DATA(DATA_IN[2]), .PIN_IN(PORT_IN[2]), .PIN_OUT(PORT_OUT[2]), .DATA_IN(DATA_OUT[2]));
  Pull_Resistor pull_resistor_3 (.node(DATA_OUT[2]));
  Transistor_Test transistor_test_4 (
    .DDR(DDR[3]), .DATA(DATA_IN[3]), .PIN_IN(PORT_IN[3]), .PIN_OUT(PORT_OUT[3]), .DATA_IN(DATA_OUT[3]));
  Pull_Resistor pull_resistor_4 (.node(DATA_OUT[3]));
  Transistor_Test transistor_test_5 (
    .DDR(DDR[4]), .DATA(DATA_IN[4]), .PIN_IN(PORT_IN[4]), .PIN_OUT(PORT_OUT[4]), .DATA_IN(DATA_OUT[4]));
  Pull_Resistor pull_resistor_5 (.node(DATA_OUT[4]));
  Transistor_Test transistor_test_6 (
    .DDR(DDR[5]), .DATA(DATA_IN[5]), .PIN_IN(PORT_IN[5]), .PIN_OUT(PORT_OUT[5]), .DATA_IN(DATA_OUT[5]));
  Pull_Resistor pull_resistor_6 (.node(DATA_OUT[5]));
  Transistor_Test transistor_test_7 (
    .DDR(DDR[6]), .DATA(DATA_IN[6]), .PIN_IN(PORT_IN[6]), .PIN_OUT(PORT_OUT[6]), .DATA_IN(DATA_OUT[6]));
  Pull_Resistor pull_resistor_7 (.node(DATA_OUT[6]));
  Transistor_Test transistor_test_8 (
    .DDR(DDR[7]), .DATA(DATA_IN[7]), .PIN_IN(PORT_IN[7]), .PIN_OUT(PORT_OUT[7]), .DATA_IN(DATA_OUT[7]));
  Pull_Resistor pull_resistor_8 (.node(DATA_OUT[7]));
endmodule

module Transistor_Test (
  input  DDR,
  input  DATA,
  input  PIN_IN,
  output PIN_OUT,
  output DATA_IN
);

  wire not_1_out;

  not not_1 (not_1_out, DDR);
  assign DATA_IN = not_1_out ? PIN_IN : 1'bz;  // Controlled_Buffer controlled_buffer_1
  assign PIN_OUT = DDR ? DATA : 1'bz;  // Controlled_Buffer controlled_buffer_2
endmodule
